# Fritzing sketch Schematic_src (saved by Fritzing 0.9.3b)
breadboards: 2

parts:
  Part2 = Adafruit T-Cobbler Plus [part_number="Adafruit #1989 and #2028"]  # not connected
  U1 = Optocoupler [package=THT]
  U2 = Optocoupler [package=THT]
  U3 = Optocoupler [package=THT]

nets:
  N1: U1.Pin_2, U1.Pin_4, U2.Pin_2, U2.Pin_4, U3.Pin_2, U3.Pin_4

custom parts:
  Adafruit T-Cobbler Plus: The Raspberry Pi has landed on the Maker World like a 40-GPIO pinned, quad-USB ported, credit card sized bomb of DIY joy. And while you can use most of our great Model B accessories by hooking up our downgrade cable, its probably a good time to upgrade your set up and accessorize using all of the 40 pins. That's why we now carry the Assembled Adafruit Pi T-Cobbler Plus - Breakout + Cable for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
